# Fritzing sketch Circuit Diagram (saved by Fritzing 0.9.4)
breadboards: 1

parts:
  U1 = NodeMCU V1.0
  Power_plug1 = Power plug
  L298N1 = L298N DC motor driver
  M1 = DC Motor
  RHT2 = Humidity and Temperature Sensor RHT03 [part_number=DHT22]
  R1 = Resistor [tolerance=±5% resistance=4.6k package=THT]

nets:
  N1: U1.D1, RHT2.Data-signal, R1.Pin_1
  N2: U1.D2, L298N1.ENA
  N3: U1.D3, L298N1.IN1
  N4: U1.D4, L298N1.IN2
  3V3: U1.3V3, RHT2.Vcc, R1.Pin_0
  GND: U1.GND, Power_plug1.GND, L298N1.GND, RHT2.GND_2
  VCC: Power_plug1.VCC, L298N1.12V
  N5: L298N1.OUT1, M1.pin_2
  N6: L298N1.OUT2, M1.pin_1

custom parts:
  NodeMCU V1.0: ESP8266 based NodeMCU
  L298N DC motor driver: 2x DC motor driver with 78M05 positive voltage regulator (7..35 V) L298N: max 46 V, 2 A Set 5 V Enable jumper to enable 5 V regultor (needed for the L298N) and +5 V output at screw terminal or supply external +5 V at screw terminal Set ENA and/or ENB to +5 V to enable motor permanently or supply ENA and/or ENB with PWM signal IN1 and IN2 set rotation directory for motor A (OUT1/OUT2) IN2 and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
